# Fritzing sketch DLP Adapter Board (saved by Fritzing 0.9.4)
circuit board: 9.77207cm x 5.61739cm
breadboards: 1

parts:
  P8 = double row female pin header, 46 pins [form="♀ (female)"]
  Raspi = double row female pin header, 40 pins [form="♀ (female)"]
  5V_in = screw terminal, 2 pins
  P9 = double row female pin header, 46 pins [form="♀ (female)"]
  IRL_520N = Basic FET N-Channel [package="TO220 [THT]"]
  HC_SR501 = screw terminal, 3 pins
  5V_out = screw terminal, 2 pins
  BH1750 = female pin header, 5 pins [form="♀ (female)"]

nets:
  N1: P8.pin1, Raspi.pin26
  N2: P8.pin2, Raspi.pin39
  N3: P8.pin3, Raspi.pin11
  N4: P8.pin4, Raspi.pin36
  N5: P8.pin5, Raspi.pin24
  N6: P8.pin6, Raspi.pin25
  N7: P8.pin7, Raspi.pin6
  N8: P8.pin8, Raspi.pin10
  N9: P8.pin9, Raspi.pin34
  N10: P8.pin10, Raspi.pin7
  N11: P8.pin11, Raspi.pin2
  N12: P8.pin16, Raspi.pin17
  N13: P8.pin31, Raspi.pin38
  N14: P8.pin37, Raspi.pin19
  N15: P8.pin38, Raspi.pin18
  N16: P8.pin39, Raspi.pin32
  N17: P8.pin40, Raspi.pin33
  N18: P8.pin41, Raspi.pin5
  N19: P8.pin42, Raspi.pin4
  N20: P8.pin43, Raspi.pin9
  N21: P8.pin44, Raspi.pin40
  N22: P8.pin45, Raspi.pin3
  N23: P8.pin46, Raspi.pin15
  N24: Raspi.pin1, 5V_in.pin2, IRL_520N.source, HC_SR501.pin2, BH1750.pin2, BH1750.pin5
  N25: Raspi.pin13, P9.pin31
  N26: Raspi.pin14, IRL_520N.gate
  N27: Raspi.pin20, HC_SR501.pin1, BH1750.pin1
  N28: Raspi.pin21, 5V_in.pin1, 5V_out.pin1
  N29: Raspi.pin28, P9.pin14, BH1750.pin4
  N30: Raspi.pin29, P9.pin33, BH1750.pin3
  N31: Raspi.pin31, HC_SR501.pin3
  N32: P9.pin1, P9.pin23, P9.pin24, P9.pin46, IRL_520N.drain, 5V_out.pin2

notes:
  1
  2
  39
  40
  45
  46
  PicturePi
  VCC
  5V
  3V3
  GND
