# Fritzing sketch PicturePi (saved by Fritzing 0.9.3b)
circuit board: 8.78906cm x 6.46799cm
breadboards: 1

parts:
  part = BeagleBone Black
  Pi = Generic double row female header - 40 pins [form="♀ (female)" package=THT]
  IC1 = IC, DIP package, 4 pins [chip_label=IC]
  +5V_in = Screw terminal - 2 pins [package=THT]
  R1 = Resistor [tolerance=±5% resistance=220 package=THT]
  +5V_out = Screw terminal - 2 pins [package=THT]

nets:
  N1: part.no_name_yet#1, part.no_name_yet#2, Pi.pin39, Pi.pin34, Pi.pin20, IC1.pin2, +5V_in.pin1, +5V_out.pin1
  N2: part.no_name_yet#19, Pi.pin18
  N3: part.no_name_yet#20, Pi.pin16
  N4: part.no_name_yet#115, Pi.pin36
  N5: part.no_name_yet#116, Pi.pin7
  N6: part.no_name_yet#127, Pi.pin3
  N7: part.no_name_yet#128, Pi.pin27
  N8: part.no_name_yet#129, Pi.pin5
  N9: part.no_name_yet#131, Pi.pin24
  N10: part.no_name_yet#132, Pi.pin21
  N11: part.no_name_yet#133, Pi.pin26
  N12: part.no_name_yet#134, Pi.pin29
  N13: part.no_name_yet#135, Pi.pin31
  N14: part.no_name_yet#136, Pi.pin10
  N15: part.no_name_yet#137, Pi.pin33
  N16: part.no_name_yet#138, Pi.pin8
  N17: part.no_name_yet#139, Pi.pin23
  N18: part.no_name_yet#140, Pi.pin32
  N19: part.no_name_yet#141, Pi.pin40
  N20: part.no_name_yet#142, Pi.pin19
  N21: part.no_name_yet#143, Pi.pin35
  N22: part.no_name_yet#144, Pi.pin38
  N23: part.no_name_yet#145, Pi.pin11
  N24: part.no_name_yet#146, Pi.pin12
  N25: Pi.pin22, R1.Pin_1
  N26: Pi.pin4, Pi.pin2, IC1.pin4, +5V_in.pin2
  N27: IC1.pin1, R1.Pin_0
  N28: IC1.pin3, +5V_out.pin2

custom parts:
  BeagleBone Black: BeagleBone Black rev. A5B
  Generic double row female header - 40 pins: Generic double row female header
